# Fritzing sketch PIR (saved by Fritzing 0.9.3b)
breadboards: 1

parts:
  PIR2 = PIR sensor
  Raspberry_Pi1 = Raspberry Pi 2
  R1 = Resistor [tolerance=±20% resistance=10k package=THT]

nets:
  VDD: PIR2.VDD, Raspberry_Pi1.5V
  N1: PIR2.SIG, R1.Pin_1
  GND: PIR2.GND, Raspberry_Pi1.GND
  N2: Raspberry_Pi1.GPIO23, R1.Pin_0
