# Fritzing sketch SoilMoistureSensor (saved by Fritzing 0.9.3b)

parts:
  Raspberry_Pi2 = Raspberry Pi 2
  Part4 = FC-28 Soil Hygrometer Module - Probe
  Part5 = FC-28 Soil Hygrometer Module

nets:
  3V3: Raspberry_Pi2.3v3, Part5.VCC
  N1: Raspberry_Pi2.GPIO17, Part5.DO
  GND: Raspberry_Pi2.GND, Part5.GND
  N2: Part4.POS, Part5.POS
  N3: Part4.NEG, Part5.NEG

custom parts:
  FC-28 Soil Hygrometer Module - Probe: The FC-28 is a soil hygrometer module that uses the Texas Instruments LM393 comparator chip to provide an analog measurement of soil humidity.
  FC-28 Soil Hygrometer Module: The FC-28 is a soil hygrometer module that uses the Texas Instruments LM393 comparator chip to provide an analog measurement of soil humidity. The digital output is high when soil moisture is over a certain threshold, as determined by adjusting the potentiometer.
